// Logisim project Knoll_Lewis_proj1.circ as structural Verilog: 13 circuits, main circuit ALU
module Arch (
  input  [7:0] A,
  input  [7:0] B,
  input  [2:0] opcode,
  output [7:0] O
);

  ALU alu_1 (.A(A), .B(B), .opcode(opcode), .O(O));  // open: cout
endmodule

module ALU (
  input  [7:0] A,
  input  [7:0] B,
  input  [2:0] opcode,
  output [7:0] O,
  output cout
);

  wire [7:0] bitand_1_o, bitor_1_o, bitshifter_1_o, bitxor_1_o, eightbitadder_1_sum, eightbitsubtractor_1_o,
       fourbitmultiplier_1_o;

  BitXOR bitxor_1 (.A(A), .B(B), .O(bitxor_1_o));
  BitAND bitand_1 (.A(A), .B(B), .O(bitand_1_o));
  BitOR bitor_1 (.A(A), .B(B), .O(bitor_1_o));
  EightBitAdder eightbitadder_1 (.A(A), .B(B), .Sum(eightbitadder_1_sum), .CarryOut(cout));  // open: FirstCarry
  EightBitSubtractor eightbitsubtractor_1 (.A(A), .B(B), .O(eightbitsubtractor_1_o));  // open: Static
  BitShifter bitshifter_1 (.I(B), .O(bitshifter_1_o));
  FourBitMultiplier fourbitmultiplier_1 (.A(A), .B(B), .O(fourbitmultiplier_1_o));  // open: Static
  Multiplexer #(.select(3), .width(8)) multiplexer_1 (
    .in0(B), .in1(bitxor_1_o), .in2(bitand_1_o), .in3(bitor_1_o), .in4(eightbitadder_1_sum),
    .in5(eightbitsubtractor_1_o), .in6(bitshifter_1_o), .in7(fourbitmultiplier_1_o), .out(O), .sel(opcode));
endmodule

module HalfAdder (
  input  A,
  input  B,
  output Sum,
  output Carry
);

  xor xor_1 (Sum, A, B);
  and and_1 (Carry, A, B);
endmodule

module FullAdder (
  input  A,
  input  B,
  input  C,
  output Sum,
  output Carry
);

  wire halfadder_1_carry, halfadder_1_sum, halfadder_2_carry;

  HalfAdder halfadder_1 (.A(B), .B(C), .Sum(halfadder_1_sum), .Carry(halfadder_1_carry));
  HalfAdder halfadder_2 (.A(A), .B(halfadder_1_sum), .Sum(Sum), .Carry(halfadder_2_carry));
  or or_1 (Carry, halfadder_2_carry, halfadder_1_carry);
endmodule

module EightBitAdder (
  input  FirstCarry,
  input  [7:0] A,
  input  [7:0] B,
  output [7:0] Sum,
  output CarryOut
);

  wire fulladder_1_carry, fulladder_2_carry, fulladder_3_carry, fulladder_4_carry, fulladder_5_carry,
       fulladder_6_carry, fulladder_7_carry;

  FullAdder fulladder_1 (.A(FirstCarry), .B(A[0]), .C(B[0]), .Sum(Sum[0]), .Carry(fulladder_1_carry));
  FullAdder fulladder_2 (.A(fulladder_7_carry), .B(A[4]), .C(B[4]), .Sum(Sum[4]), .Carry(fulladder_2_carry));
  FullAdder fulladder_3 (.A(fulladder_1_carry), .B(A[1]), .C(B[1]), .Sum(Sum[1]), .Carry(fulladder_3_carry));
  FullAdder fulladder_4 (.A(fulladder_2_carry), .B(A[5]), .C(B[5]), .Sum(Sum[5]), .Carry(fulladder_4_carry));
  FullAdder fulladder_5 (.A(fulladder_3_carry), .B(A[2]), .C(B[2]), .Sum(Sum[2]), .Carry(fulladder_5_carry));
  FullAdder fulladder_6 (.A(fulladder_4_carry), .B(A[6]), .C(B[6]), .Sum(Sum[6]), .Carry(fulladder_6_carry));
  FullAdder fulladder_7 (.A(fulladder_5_carry), .B(A[3]), .C(B[3]), .Sum(Sum[3]), .Carry(fulladder_7_carry));
  FullAdder fulladder_8 (.A(fulladder_6_carry), .B(A[7]), .C(B[7]), .Sum(Sum[7]), .Carry(CarryOut));
endmodule

module BitXOR (
  input  [7:0] A,
  input  [7:0] B,
  output [7:0] O
);

  xor xor_1 (O[0], A[0], B[0]);
  xor xor_2 (O[1], A[1], B[1]);
  xor xor_3 (O[4], A[4], B[4]);
  xor xor_4 (O[5], A[5], B[5]);
  xor xor_5 (O[2], A[2], B[2]);
  xor xor_6 (O[6], A[6], B[6]);
  xor xor_7 (O[3], A[3], B[3]);
  xor xor_8 (O[7], A[7], B[7]);
endmodule

module BitAND (
  input  [7:0] A,
  input  [7:0] B,
  output [7:0] O
);

  and and_1 (O[0], A[0], B[0]);
  and and_2 (O[1], A[1], B[1]);
  and and_3 (O[4], A[4], B[4]);
  and and_4 (O[5], A[5], B[5]);
  and and_5 (O[2], A[2], B[2]);
  and and_6 (O[6], A[6], B[6]);
  and and_7 (O[3], A[3], B[3]);
  and and_8 (O[7], A[7], B[7]);
endmodule

module BitOR (
  input  [7:0] A,
  input  [7:0] B,
  output [7:0] O
);

  or or_1 (O[0], A[0], B[0]);
  or or_2 (O[1], A[1], B[1]);
  or or_3 (O[4], A[4], B[4]);
  or or_4 (O[5], A[5], B[5]);
  or or_5 (O[2], A[2], B[2]);
  or or_6 (O[6], A[6], B[6]);
  or or_7 (O[3], A[3], B[3]);
  or or_8 (O[7], A[7], B[7]);
endmodule

module BitSubtractor (
  input  BorrowIn,
  input  A,
  input  B,
  output O,
  output BorrowOut
);

  wire and_1_out, and_2_out, not_1_out, not_2_out, xor_1_out;

  not not_1 (not_1_out, A);
  xor xor_1 (xor_1_out, A, B);
  and and_1 (and_1_out, not_1_out, B);
  not not_2 (not_2_out, xor_1_out);
  and and_2 (and_2_out, BorrowIn, not_2_out);
  xor xor_2 (O, xor_1_out, BorrowIn);
  or or_1 (BorrowOut, and_2_out, and_1_out);
endmodule

module EightBitSubtractor (
  input  Static,
  input  [7:0] A,
  input  [7:0] B,
  output [7:0] O
);

  wire fulladder_1_carry, fulladder_2_carry, fulladder_3_carry, fulladder_4_carry, fulladder_5_carry,
       fulladder_6_carry, fulladder_7_carry, not_1_out, not_2_out, not_3_out, not_4_out, not_5_out,
       not_6_out, not_7_out, not_8_out, not_9_out;

  not not_1 (not_1_out, Static);
  not not_2 (not_2_out, B[0]);
  not not_3 (not_3_out, B[4]);
  FullAdder fulladder_1 (.A(not_1_out), .B(A[0]), .C(not_2_out), .Sum(O[0]), .Carry(fulladder_1_carry));
  not not_4 (not_4_out, B[1]);
  FullAdder fulladder_2 (.A(fulladder_7_carry), .B(A[4]), .C(not_3_out), .Sum(O[4]), .Carry(fulladder_2_carry));
  not not_5 (not_5_out, B[5]);
  FullAdder fulladder_3 (.A(fulladder_1_carry), .B(A[1]), .C(not_4_out), .Sum(O[1]), .Carry(fulladder_3_carry));
  not not_6 (not_6_out, B[2]);
  FullAdder fulladder_4 (.A(fulladder_2_carry), .B(A[5]), .C(not_5_out), .Sum(O[5]), .Carry(fulladder_4_carry));
  not not_7 (not_7_out, B[6]);
  not not_8 (not_8_out, B[3]);
  not not_9 (not_9_out, B[7]);
  FullAdder fulladder_5 (.A(fulladder_3_carry), .B(A[2]), .C(not_6_out), .Sum(O[2]), .Carry(fulladder_5_carry));
  FullAdder fulladder_6 (.A(fulladder_4_carry), .B(A[6]), .C(not_7_out), .Sum(O[6]), .Carry(fulladder_6_carry));
  FullAdder fulladder_7 (.A(fulladder_5_carry), .B(A[3]), .C(not_8_out), .Sum(O[3]), .Carry(fulladder_7_carry));
  FullAdder fulladder_8 (.A(fulladder_6_carry), .B(A[7]), .C(not_9_out), .Sum(O[7]));  // open: Carry
endmodule

module BitShifter (
  input  [7:0] I,
  output [7:0] O
);


  assign O = {I[0], I[7:1]};
endmodule

module FourBitAdder (
  input  FirstCarry,
  input  [3:0] A,
  input  [3:0] B,
  output [3:0] Sum,
  output CarryOut
);

  wire fulladder_1_carry, fulladder_2_carry, fulladder_3_carry;

  FullAdder fulladder_1 (.A(FirstCarry), .B(A[0]), .C(B[0]), .Sum(Sum[0]), .Carry(fulladder_1_carry));
  FullAdder fulladder_2 (.A(fulladder_1_carry), .B(A[1]), .C(B[1]), .Sum(Sum[1]), .Carry(fulladder_2_carry));
  FullAdder fulladder_3 (.A(fulladder_2_carry), .B(A[2]), .C(B[2]), .Sum(Sum[2]), .Carry(fulladder_3_carry));
  FullAdder fulladder_4 (.A(fulladder_3_carry), .B(A[3]), .C(B[3]), .Sum(Sum[3]), .Carry(CarryOut));
endmodule

module FourBitMultiplier (
  input  [7:0] A,
  input  [7:0] B,
  input  Static,
  output [7:0] O
);

  wire [3:0] and_8_out, and_12_out, and_16_out;
  wire [3:1] and_4_out, fourbitadder_1_sum, fourbitadder_2_sum;
  wire [3:3] fourbitadder_1_carryout, fourbitadder_2_carryout;

  and and_1 (O[0], A[0], B[0]);
  and and_2 (and_4_out[3], A[1], B[0]);
  and and_3 (and_4_out[2], A[2], B[0]);
  and and_4 (and_4_out[1], A[3], B[0]);
  and and_5 (and_8_out[3], A[0], B[1]);
  and and_6 (and_8_out[2], A[1], B[1]);
  and and_7 (and_8_out[1], A[2], B[1]);
  and and_8 (and_8_out[0], A[3], B[1]);
  and and_9 (and_12_out[3], A[0], B[2]);
  and and_10 (and_12_out[2], A[1], B[2]);
  and and_11 (and_12_out[1], A[2], B[2]);
  and and_12 (and_12_out[0], A[3], B[2]);
  and and_13 (and_16_out[3], A[0], B[3]);
  and and_14 (and_16_out[2], A[1], B[3]);
  and and_15 (and_16_out[1], A[2], B[3]);
  and and_16 (and_16_out[0], A[3], B[3]);
  FourBitAdder fourbitadder_1 (
    .A({and_4_out, Static}), .B(and_8_out), .Sum({fourbitadder_1_sum, O[1]}),
    .CarryOut(fourbitadder_1_carryout[3]));  // open: FirstCarry
  FourBitAdder fourbitadder_2 (
    .A({fourbitadder_1_carryout[3], fourbitadder_1_sum}), .B(and_12_out), .Sum({fourbitadder_2_sum, O[2]}),
    .CarryOut(fourbitadder_2_carryout[3]));  // open: FirstCarry
  FourBitAdder fourbitadder_3 (
    .A({fourbitadder_2_carryout[3], fourbitadder_2_sum}), .B(and_16_out), .Sum(O[6:3]), .CarryOut(O[7]));  // open: FirstCarry
endmodule
